# Fritzing sketch arduino (saved by Fritzing 0.7.12b)
breadboards: 1

parts:
  ATTiny85 = attiny85 [package=dip]
  DS18S20 = LM35 Temperature Sensor [package="TO92 [THT]"]
  R1_4_7KOhm = 470 Ω Resistor [package=THT]
  Serial = Generic male header - 4 pins [package=THT]
  LED = LED - 3mm [color="Red (633nm)" package="3 mm [THT]"]

nets:
  N1: ATTiny85.Pin_3, LED.anode
  N2: ATTiny85.Pin_4, DS18S20.+Vs, Serial.pin4, LED.cathode
  N3: ATTiny85.Pin_5, DS18S20.Vout, R1_4_7KOhm.Pin_0
  N4: ATTiny85.Pin_6, Serial.pin2
  N5: ATTiny85.Pin_7, Serial.pin3
  N6: ATTiny85.Pin_8, DS18S20.GND, R1_4_7KOhm.Pin_1, Serial.pin1
